# Fritzing sketch controlservox1_rxCaJHzZAd (saved by Fritzing 0.9.3b)
circuit board: 6.88566cm x 5.36311cm
breadboards: 1

parts:
  Joystick = Thumb Joystick
  TILT = Basic Servo
  PAN = Basic Servo
  Arduino_UNO = Arduino Uno (Rev3)

nets:
  GND: Joystick.GND, TILT.gnd, PAN.gnd
  N1: Joystick.HORZ, Arduino_UNO.A1
  N2: Joystick.VERT, Arduino_UNO.A0
  5V: Joystick.VCC, TILT.vcc, PAN.vcc, Arduino_UNO.5V
  N3: TILT.pulse, Arduino_UNO.D10_PWM/SS
  N4: PAN.pulse, Arduino_UNO.D9_PWM

notes:
  VER OR VRX TO A0
  HOR OR VRY TO A1
  GND TO GND
  +5V TO 5V
  TILT SERVO TO PWM 10
  PAN SERVO TO PWM 9
  Control Servos with a Thumbstick , Control Servos with a Thumbstick
  Thomas Kroon
